// Logisim project SEGA 315-5309.circ as structural Verilog: 4 circuits, main circuit main
module main (
  input  VCLK,
  input  nM3,
  input  nSRES,
  input  TEST,
  input  NTSC,
  input  ZA0,
  input  ZA1,
  input  ZA2,
  input  ZA3,
  input  ZA4,
  input  ZA5,
  input  ZA6,
  input  ZA7,
  input  A0,
  input  A1,
  input  A2,
  input  A3,
  input  A4,
  input  A5,
  input  A6,
  input  A7,
  input  D0,
  input  D1,
  input  D2,
  input  D3,
  input  D4,
  input  D5,
  input  D6,
  input  D7,
  input  D8,
  input  D9,
  input  D10,
  input  D11,
  input  D12,
  input  D13,
  input  D14,
  input  D15,
  input  ZD0,
  input  ZD1,
  input  ZD2,
  input  ZD3,
  input  ZD4,
  input  ZD5,
  input  ZD6,
  input  ZD7,
  input  EM31,
  input  EM32,
  input  EM33,
  input  EM34,
  input  EM36,
  input  EM38,
  input  EM37,
  input  EM11,
  input  EM12,
  input  EM13,
  input  EM14,
  input  EM16,
  input  EM18,
  input  EM17,
  input  EM21,
  input  EM22,
  input  EM23,
  input  EM24,
  input  EM26,
  input  EM28,
  input  EM27,
  input  nVTOZ,
  input  nZTOV,
  input  nIO,
  input  FREQ,
  input  LANG,
  input  nCAS0,
  input  nLWR,
  input  nDISK,
  input  nFRES,
  output FRES,
  output D0_2,
  output D1_2,
  output D2_2,
  output D3_2,
  output D4_2,
  output D5_2,
  output D6_2,
  output D7_2,
  output D8_2,
  output D9_2,
  output D10_2,
  output D11_2,
  output D12_2,
  output D13_2,
  output D14_2,
  output D15_2,
  output ZD0_2,
  output ZD1_2,
  output ZD2_2,
  output ZD3_2,
  output ZD4_2,
  output ZD5_2,
  output ZD6_2,
  output ZD7_2,
  output EM31_2,
  output EM32_2,
  output EM33_2,
  output EM34_2,
  output EM36_2,
  output EM38_2,
  output EM37_2,
  output EM11_2,
  output EM12_2,
  output EM13_2,
  output EM14_2,
  output EM16_2,
  output EM18_2,
  output EM17_2,
  output EM21_2,
  output EM22_2,
  output EM23_2,
  output EM24_2,
  output EM26_2,
  output EM28_2,
  output EM27_2,
  output nHL
);

  wire _17_q, _47_q, _78_nq, _79_out, _80_co, _80_nq, _81_co, _81_nq, _81_q, _113_q, _114_out, _117_out,
       _120_out, _128_out, _129_co, _129_nq, _130_co, _130_nq, _132_out, _133_co, _133_nq, _134_nq, _165_q,
       _175_out, _176_out, _177_q, _179_q, _182_q, _188_co, _188_nq, _212_q, _218_out, _220_qn, _221_out,
       _222_out, _223_out, _224_out, _226_out, _229_q, _231_q, _234_q, _236_q, _237_out, _242_out, _244_q,
       _246_nq, _249_nq, _250_nq, _251_nq, _252_nq, _297_nq, _304_nq, _319_nq, _325_out, _326_out, _335_out,
       _342_out, _344_q, _346_q, _349_out, _354_qn, _393_out, _394_out, _395_out, _398_out, _401_out,
       _403_out, _404_out, _406_out, _407_out, _408_q, _409_out, _410_q, _410_qn, _411_q, _411_qn, _412_out,
       _413_out, _414_q, _414_qn, _415_out, _416_q, _416_qn, _417_out, _418_q, _418_qn, _419_q, _420_out,
       _429_q, _432_out, _463_q, _463_qn, _464_q, _464_qn, _465_out, _466_q, _466_qn, _468_q, _468_qn,
       _469_out, _470_out, _471_out, _472_out, _473_out, _474_out, _475_out, _476_out, _477_out, _478_out,
       _479_out, _480_out, _481_out, _482_out, _483_out, _484_out, _485_out, _547_out, _548_out, _549_out,
       _550_out, _551_out, _552_out, _553_out, _554_out, _555_out, _556_out, _557_q, _557_qn, _558_out,
       _559_q, _559_qn, _560_out, _561_out, _562_out, _563_out, _616_q, _616_qn, _617_out, _618_out,
       _619_out, _642_out, _643_out, _644_out, _645_out, _666_out, _676_out, _677_out, _681_out, _682_out,
       _684_out, _694_out, _695_out, _697_out, d_ff_5_q, d_ff_6_q, d_ff_7_q, d_ff_8_q, d_ff_9_q, d_ff_10_q,
       d_ff_11_q, d_ff_12_q, DIV0, DIV1, DIV2, DIV3, DIV4, DIV5, DIV6, FRES_t, multiplexer_3_out,
       multiplexer_4_out, multiplexer_5_out, multiplexer_6_out, multiplexer_7_out, multiplexer_8_out,
       multiplexer_9_out, multiplexer_10_out, multiplexer_11_out, not_2_out, not_3_out, not_4_out, not_5_out,
       not_6_out, not_7_out, not_8_out, not_9_out, not_10_out, not_11_out, not_12_out, not_13_out,
       not_14_out, PB4_o, PB5_i, UCLK1, undriven, undriven_2, undriven_3;
  wire [1:0] d_ff_1_q;
  wire [7:0] _249_q, undriven_4;

  not _666 (_666_out, NTSC);
  and _645 (_645_out, _132_out, 1'b1);
  and _642 (_642_out, _645_out, _79_out);
  and _128 (_128_out, 1'b1, _644_out, 1'b1);
  and _242 (_242_out, 1'b1, _645_out, _644_out);
  nor _643 (_643_out, FRES_t, _642_out);
  buf _644 (_644_out, _643_out);
  D_Flip_Flop _595 (.clk(VCLK), .D(nSRES), .Qn(FRES));  // open: Q, preset, en, reset
  _1_bit_cnt _129 (
    .C(VCLK), .CIN(_128_out), .VAL(_666_out), .nLD(_644_out), .nRES(1'b1), .nQ(_129_nq), .CO(_129_co));  // open: Q
  _1_bit_cnt _130 (
    .C(VCLK), .CIN(_129_co), .VAL(1'b0), .nLD(_644_out), .nRES(1'b1), .nQ(_130_nq), .CO(_130_co));  // open: Q
  _1_bit_cnt _133 (
    .C(VCLK), .CIN(_130_co), .VAL(1'b1), .nLD(_644_out), .nRES(1'b1), .nQ(_133_nq), .CO(_133_co));  // open: Q
  _1_bit_cnt _134 (.C(VCLK), .CIN(_133_co), .VAL(1'b1), .nLD(_644_out), .nRES(1'b1), .nQ(_134_nq));  // open: Q, CO
  _1_bit_cnt _188 (
    .C(VCLK), .CIN(_242_out), .VAL(1'b1), .nLD(_644_out), .nRES(1'b1), .nQ(_188_nq), .CO(_188_co));  // open: Q
  _1_bit_cnt _80 (
    .C(VCLK), .CIN(_188_co), .VAL(1'b0), .nLD(_644_out), .nRES(1'b1), .nQ(_80_nq), .CO(_80_co));  // open: Q
  _1_bit_cnt _81 (.C(VCLK), .CIN(_80_co), .VAL(1'b0), .nLD(_644_out), .nRES(1'b1), .Q(_81_q), .nQ(_81_nq), .CO(_81_co));
  _1_bit_cnt _78 (.C(VCLK), .CIN(_81_co), .VAL(1'b1), .nLD(_644_out), .nRES(1'b1), .nQ(_78_nq));  // open: Q, CO
  buf _376 (FRES_t, FRES);
  nor _132 (_132_out, _134_nq, _133_nq, _130_nq, _129_nq);
  nor _79 (_79_out, _78_nq, _81_nq, _80_nq, _188_nq);
  Multiplexer #(.disabled(0), .enable("false")) multiplexer_1 (.in0(_81_q), .in1(VCLK), .out(DIV0), .sel(TEST));
  // Buffer _237 has open pins: in=open, out=_237_out
  T_Flip_Flop _239 (.clk(DIV0), .T(_237_out), .Q(DIV1));  // open: Qn, preset, reset, en
  T_Flip_Flop _240 (.clk(DIV1), .T(_237_out), .Q(DIV2));  // open: Qn, preset, reset, en
  T_Flip_Flop _244 (.clk(DIV2), .T(_237_out), .Q(_244_q));  // open: Qn, preset, reset, en
  T_Flip_Flop _243 (.clk(_244_q), .T(_237_out), .Q(DIV3));  // open: Qn, preset, reset, en
  T_Flip_Flop _238 (.clk(DIV3), .T(_237_out), .Q(DIV4));  // open: Qn, preset, reset, en
  T_Flip_Flop _347 (.clk(DIV4), .T(_237_out), .Q(DIV5));  // open: Qn, preset, reset, en
  T_Flip_Flop _346 (.clk(DIV5), .T(_237_out), .Q(_346_q));  // open: Qn, preset, reset, en
  T_Flip_Flop _345 (.clk(_346_q), .T(_237_out), .Q(DIV6));  // open: Qn, preset, reset, en
  not _407 (_407_out, undriven);
  not _325 (_325_out, undriven_2);
  not _326 (_326_out, undriven_3);
  not _401 (_401_out, _407_out);
  not _398 (_398_out, _325_out);
  not _406 (_406_out, _326_out);
  // NOT_Gate not_1 is placed but not wired
  // NOR_Gate _335 has open pins: out=_335_out
  // NAND_Gate _405 has open pins: in0=_406_out, in1=_407_out, in2=_398_out, in3=_335_out, out=open
  nand _404 (_404_out, _326_out, _407_out, _398_out, _335_out);
  nand _403 (_403_out, _406_out, _407_out, _325_out, _335_out);
  // NAND_Gate _402 has open pins: in0=_326_out, in1=_407_out, in2=_325_out, in3=_335_out, out=open
  // NAND_Gate _400 has open pins: in0=_326_out, in1=_401_out, in2=_325_out, in3=_335_out, out=open
  // NAND_Gate _399 has open pins: in0=_326_out, in1=_401_out, in2=_398_out, in3=_335_out, out=open
  // NAND_Gate _397 has open pins: in0=_406_out, in1=_401_out, in2=_398_out, in3=_335_out, out=open
  // NAND_Gate _396 has open pins: in0=_406_out, in1=_401_out, in2=_325_out, in3=_335_out, out=open
  S_latch _249 (.EN(not_2_out), .D(undriven_4[0]), .Q(_249_q[0]), .nQ(_249_nq));
  S_latch _304 (.EN(not_2_out), .D(undriven_4[1]), .Q(_249_q[1]), .nQ(_304_nq));
  S_latch _250 (.EN(not_2_out), .D(undriven_4[2]), .Q(_249_q[2]), .nQ(_250_nq));
  S_latch _246 (.EN(not_2_out), .D(undriven_4[3]), .Q(_249_q[3]), .nQ(_246_nq));
  S_latch _252 (.EN(not_2_out), .D(undriven_4[4]), .Q(_249_q[4]), .nQ(_252_nq));
  S_latch _319 (.EN(not_2_out), .D(undriven_4[5]), .Q(_249_q[5]), .nQ(_319_nq));
  S_latch _251 (.EN(not_2_out), .D(undriven_4[6]), .Q(_249_q[6]), .nQ(_251_nq));
  S_latch _297 (.EN(not_2_out), .D(undriven_4[7]), .Q(_249_q[7]), .nQ(_297_nq));
  not not_2 (not_2_out, _404_out);
  D_Flip_Flop d_ff_1 (.Q(d_ff_1_q[0]));  // open: clk, D, Qn, preset, en, reset
  D_Flip_Flop d_ff_2 (.Q(d_ff_1_q[1]));  // open: clk, D, Qn, preset, en, reset
  D_Flip_Flop d_ff_3 ();  // open: clk, D, Q, Qn, preset, en, reset
  D_Flip_Flop _47 (.Q(_47_q));  // open: clk, D, Qn, preset, en, reset
  D_Flip_Flop d_ff_4 ();  // open: clk, D, Q, Qn, preset, en, reset
  Multiplexer #(.select(2), .disabled(0), .enable("false")) multiplexer_2 (
    .in0(DIV0), .in1(DIV2), .in2(DIV1), .in3(DIV3), .out(UCLK1), .sel(d_ff_1_q));
  Multiplexer #(.select(2), .disabled(0), .enable("false")) multiplexer_3 (
    .in0(DIV3), .in1(DIV5), .in2(DIV4), .in3(DIV6), .out(multiplexer_3_out), .sel(d_ff_1_q));
  // NAND_Gate _412 has open pins: out=_412_out
  not not_3 (not_3_out, _412_out);
  not not_4 (not_4_out, not_3_out);
  Multiplexer #(.disabled(0), .enable("false")) multiplexer_4 (
    .in0(_249_nq), .in1(_179_q), .out(multiplexer_4_out), .sel(not_4_out));
  Multiplexer #(.disabled(0), .enable("false")) multiplexer_5 (
    .in0(_304_nq), .in1(_182_q), .out(multiplexer_5_out), .sel(not_4_out));
  Multiplexer #(.disabled(0), .enable("false")) multiplexer_6 (
    .in0(_250_nq), .in1(_229_q), .out(multiplexer_6_out), .sel(not_4_out));
  Multiplexer #(.disabled(0), .enable("false")) multiplexer_7 (
    .in0(_246_nq), .in1(_231_q), .out(multiplexer_7_out), .sel(not_4_out));
  Multiplexer #(.disabled(0), .enable("false")) multiplexer_8 (
    .in0(_252_nq), .in1(_234_q), .out(multiplexer_8_out), .sel(not_4_out));
  Multiplexer #(.disabled(0), .enable("false")) multiplexer_9 (
    .in0(_319_nq), .in1(_236_q), .out(multiplexer_9_out), .sel(not_4_out));
  Multiplexer #(.disabled(0), .enable("false")) multiplexer_10 (
    .in0(_251_nq), .in1(_344_q), .out(multiplexer_10_out), .sel(not_4_out));
  Multiplexer #(.disabled(0), .enable("false")) multiplexer_11 (
    .in0(_297_nq), .in1(1'b0), .out(multiplexer_11_out), .sel(not_4_out));
  or _342 (_342_out, multiplexer_3_out, 1'b0);
  D_Flip_Flop _177 (.clk(_342_out), .D(multiplexer_4_out), .Q(_177_q), .reset(not_5_out));  // open: Qn, preset, en
  D_Flip_Flop _179 (.clk(_342_out), .D(multiplexer_5_out), .Q(_179_q), .reset(not_5_out));  // open: Qn, preset, en
  D_Flip_Flop _182 (.clk(_342_out), .D(multiplexer_6_out), .Q(_182_q), .reset(not_5_out));  // open: Qn, preset, en
  D_Flip_Flop _229 (.clk(_342_out), .D(multiplexer_7_out), .Q(_229_q), .reset(not_5_out));  // open: Qn, preset, en
  D_Flip_Flop _231 (.clk(_342_out), .D(multiplexer_8_out), .Q(_231_q), .reset(not_5_out));  // open: Qn, preset, en
  D_Flip_Flop _234 (.clk(_342_out), .D(multiplexer_9_out), .Q(_234_q), .reset(not_5_out));  // open: Qn, preset, en
  D_Flip_Flop _236 (.clk(_342_out), .D(multiplexer_10_out), .Q(_236_q), .reset(not_5_out));  // open: Qn, preset, en
  D_Flip_Flop _344 (.clk(_342_out), .D(multiplexer_11_out), .Q(_344_q), .reset(not_5_out));  // open: Qn, preset, en
  // NOR_Gate _224 has open pins: out=_224_out
  not _176 (_176_out, _177_q);
  not not_5 (not_5_out, _47_q);
  and _175 (_175_out, _412_out, _176_out);
  or _223 (_223_out, _410_q, _224_out);
  not _470 (_470_out, _224_out);
  buf _222 (_222_out, _220_qn);  // OR_Gate
  D_Flip_Flop _113 (.clk(multiplexer_3_out), .D(_175_out), .Q(_113_q), .preset(not_5_out));  // open: Qn, en, reset
  D_Flip_Flop _17 (.Q(_17_q));  // open: clk, D, Qn, preset, en, reset
  buf _395 (_395_out, FRES_t);
  not not_6 (not_6_out, _395_out);
  nand _472 (_472_out, _410_q, _464_q);
  nand _473 (_473_out, _410_q, _463_q);
  nand _474 (_474_out, _410_q, _468_qn);
  nand _465 (_465_out, _464_qn, _410_qn, _463_qn, _468_q);
  nand _551 (_551_out, _468_q, _463_qn);
  nand _552 (_552_out, _463_q, _468_qn);
  nand _548 (_548_out, _463_q, _464_q);
  nand _550 (_550_out, _468_q, _463_qn, _464_qn);
  nand _549 (_549_out, _468_qn, _464_q);
  nor _469 (_469_out, _468_q, _224_out);
  and _114 (_114_out, _113_q, _47_q);
  not _117 (_117_out, _47_q);
  and _120 (_120_out, _117_out, _17_q);
  D_Flip_Flop _429 (.Q(_429_q));  // open: clk, D, Qn, preset, en, reset
  D_Flip_Flop _410 (.clk(UCLK1), .D(_471_out), .Q(_410_q), .Qn(_410_qn), .preset(not_6_out));  // open: en, reset
  nand _553 (_553_out, _470_out, _551_out, _552_out);
  nand _221 (_221_out, _223_out, _222_out);
  or _119 (PB4_o, _114_out, _120_out);
  nand _471 (_471_out, _472_out, _473_out, _474_out, _465_out, _470_out, 1'b1);
  nand _547 (_547_out, _470_out, _548_out, _550_out, _549_out);
  D_Flip_Flop _463 (.clk(UCLK1), .D(_553_out), .Q(_463_q), .Qn(_463_qn), .preset(not_6_out));  // open: en, reset
  buf _420 (_420_out, FRES_t);
  nand _415 (_415_out, _414_qn, _411_q, _418_qn, _416_q);
  nand _478 (_478_out, _414_q, _411_q);
  nand _477 (_477_out, _418_q, _411_q);
  nand _479 (_479_out, _418_q, _414_q);
  nand _413 (_413_out, _429_q, _418_qn, _411_qn);
  nand _485 (_485_out, _411_q, _416_q, _414_q);
  nand _480 (_480_out, _418_q, _414_q, _411_qn);
  nand _484 (_484_out, _416_q, _418_q, _411_q);
  nand _481 (_481_out, _418_qn, _411_q);
  nand _417 (_417_out, _416_qn, _414_qn, _411_q, _418_qn);
  not not_7 (not_7_out, _420_out);
  D_Flip_Flop _464 (.clk(UCLK1), .D(_547_out), .Q(_464_q), .Qn(_464_qn), .preset(not_6_out));  // open: en, reset
  not _349 (_349_out, multiplexer_3_out);
  D_Flip_Flop _411 (
    .clk(multiplexer_3_out), .D(_476_out), .Q(_411_q), .Qn(_411_qn), .preset(not_7_out));  // open: en, reset
  nand _476 (_476_out, _415_out, _478_out, _477_out, _479_out);
  nand _475 (_475_out, _479_out, _415_out, _413_out);
  nand _483 (_483_out, _485_out, _413_out, _480_out, _484_out);
  nand _482 (_482_out, _413_out, _480_out, _481_out);
  J_K_Flip_Flop #(.trigger("falling")) _354 (.clk(_349_out), .Qn(_354_qn));  // open: J, K, Q, preset, en, reset
  D_Flip_Flop _468 (.clk(UCLK1), .D(_469_out), .Q(_468_q), .Qn(_468_qn), .reset(not_6_out));  // open: preset, en
  D_Flip_Flop _414 (
    .clk(multiplexer_3_out), .D(_475_out), .Q(_414_q), .Qn(_414_qn), .preset(not_7_out));  // open: en, reset
  D_Flip_Flop _220 (.clk(UCLK1), .D(_221_out), .Qn(_220_qn), .reset(not_6_out));  // open: Q, preset, en
  D_Flip_Flop _416 (
    .clk(multiplexer_3_out), .D(_483_out), .Q(_416_q), .Qn(_416_qn), .preset(not_7_out));  // open: en, reset
  buf _432 (_432_out, FRES);
  D_Flip_Flop _165 (.clk(_403_out), .Q(_165_q));  // open: D, Qn, preset, en, reset
  D_Flip_Flop _212 (.clk(UCLK1), .D(PB5_i), .Q(_212_q), .preset(not_8_out));  // open: Qn, en, reset
  not not_8 (not_8_out, _165_q);
  not not_9 (not_9_out, _354_qn);
  not not_10 (not_10_out, _432_out);
  D_Flip_Flop _418 (
    .clk(multiplexer_3_out), .D(_482_out), .Q(_418_q), .Qn(_418_qn), .reset(not_7_out));  // open: preset, en
  not _226 (_226_out, _212_q);
  D_Flip_Flop _426 (.clk(_419_q), .D(1'b0), .preset(not_9_out), .reset(not_10_out));  // open: Q, Qn, en
  D_Flip_Flop _419 (.clk(multiplexer_3_out), .D(_417_out), .Q(_419_q), .reset(not_7_out));  // open: Qn, preset, en
  buf _393 (_393_out, FRES_t);
  not not_11 (not_11_out, _393_out);
  nand _618 (_618_out, _466_q, _559_q, _616_q);
  nand _619 (_619_out, _557_q, _616_q, _466_q);
  nand _218 (_218_out, _226_out, _220_qn, _557_qn, _466_qn);
  nand _555 (_555_out, _466_q, _557_qn, _616_q, _559_qn);
  nand _556 (_556_out, _466_q, _559_q, _557_qn);
  nand _562 (_562_out, _466_q, _557_q, _559_q);
  nand _563 (_563_out, _557_q, _466_q);
  nand _554 (_554_out, _466_q, _557_qn, _616_qn, _559_qn);
  D_Flip_Flop _616 (.clk(_410_qn), .D(_617_out), .Q(_616_q), .Qn(_616_qn), .reset(not_11_out));  // open: preset, en
  and _394 (_394_out, 1'b1, _212_q);
  nand _617 (_617_out, _618_out, _619_out, _218_out, _554_out);
  nand _558 (_558_out, _554_out, _555_out, _218_out, _556_out);
  nand _560 (_560_out, _554_out, _555_out, _562_out, _218_out);
  nand _561 (_561_out, _555_out, _218_out, _563_out, _556_out);
  D_Flip_Flop _557 (.clk(_410_qn), .D(_558_out), .Q(_557_q), .Qn(_557_qn), .reset(not_11_out));  // open: preset, en
  not not_12 (not_12_out, _165_q);
  not not_13 (not_13_out, _165_q);
  D_Flip_Flop _559 (.clk(_410_qn), .D(_560_out), .Q(_559_q), .Qn(_559_qn), .reset(not_11_out));  // open: preset, en
  D_Flip_Flop d_ff_5 (.clk(_410_qn), .D(_394_out), .Q(d_ff_5_q), .reset(not_12_out));  // open: Qn, preset, en
  D_Flip_Flop d_ff_6 (.clk(_410_qn), .D(d_ff_5_q), .Q(d_ff_6_q), .reset(not_12_out));  // open: Qn, preset, en
  D_Flip_Flop d_ff_7 (.clk(_410_qn), .D(d_ff_6_q), .Q(d_ff_7_q), .reset(not_12_out));  // open: Qn, preset, en
  D_Flip_Flop d_ff_8 (.clk(_410_qn), .D(d_ff_7_q), .Q(d_ff_8_q), .reset(not_12_out));  // open: Qn, preset, en
  D_Flip_Flop d_ff_9 (.clk(_410_qn), .D(d_ff_8_q), .Q(d_ff_9_q), .reset(not_13_out));  // open: Qn, preset, en
  D_Flip_Flop d_ff_10 (.clk(_410_qn), .D(d_ff_9_q), .Q(d_ff_10_q), .reset(not_13_out));  // open: Qn, preset, en
  D_Flip_Flop d_ff_11 (.clk(_410_qn), .D(d_ff_10_q), .Q(d_ff_11_q), .reset(not_13_out));  // open: Qn, preset, en
  D_Flip_Flop d_ff_12 (.clk(_410_qn), .D(d_ff_11_q), .Q(d_ff_12_q), .reset(not_13_out));  // open: Qn, preset, en
  D_Flip_Flop _466 (.clk(_410_qn), .D(_561_out), .Q(_466_q), .Qn(_466_qn), .reset(not_11_out));  // open: preset, en
  RC_DELAY _677 (.IN(d_ff_5_q), .OUT(_677_out));
  RC_DELAY _684 (.IN(d_ff_6_q), .OUT(_684_out));
  RC_DELAY _676 (.IN(d_ff_7_q), .OUT(_676_out));
  RC_DELAY _681 (.IN(d_ff_8_q), .OUT(_681_out));
  RC_DELAY _694 (.IN(d_ff_9_q), .OUT(_694_out));
  RC_DELAY _697 (.IN(d_ff_10_q), .OUT(_697_out));
  RC_DELAY _682 (.IN(d_ff_11_q), .OUT(_682_out));
  RC_DELAY _695 (.IN(d_ff_12_q), .OUT(_695_out));
  D_Flip_Flop _408 (.clk(_410_qn), .D(_554_out), .Q(_408_q), .preset(not_11_out));  // open: Qn, en, reset
  D_Flip_Flop d_ff_13 ();  // open: clk, D, Q, Qn, preset, en, reset
  or _409 (_409_out, _410_qn, _408_q);
  D_Flip_Flop d_ff_14 ();  // open: clk, D, Q, Qn, preset, en, reset
  D_Flip_Flop _390 (.clk(_409_out), .D(_677_out), .reset(not_14_out));  // open: Q, Qn, preset, en
  D_Flip_Flop _274 (.clk(_409_out), .D(_684_out), .reset(not_14_out));  // open: Q, Qn, preset, en
  D_Flip_Flop _391 (.clk(_409_out), .D(_676_out), .reset(not_14_out));  // open: Q, Qn, preset, en
  D_Flip_Flop _318 (.clk(_409_out), .D(_681_out), .reset(not_14_out));  // open: Q, Qn, preset, en
  D_Flip_Flop _216 (.clk(_409_out), .D(_694_out), .reset(not_14_out));  // open: Q, Qn, preset, en
  D_Flip_Flop _202 (.clk(_409_out), .D(_697_out), .reset(not_14_out));  // open: Q, Qn, preset, en
  D_Flip_Flop _315 (.clk(_409_out), .D(_682_out), .reset(not_14_out));  // open: Q, Qn, preset, en
  D_Flip_Flop _208 (.clk(_409_out), .D(_695_out), .reset(not_14_out));  // open: Q, Qn, preset, en
  not not_14 (not_14_out, 1'b1);
  // NOT_Gate not_15 is placed but not wired

  // Other names for the same wires on the sheet: FRES0 = FRES

  // Notes on the sheet:
  //   248
  //   !
  //   SEGA 315-5309
  //   NC
  //   NC
  //   NC
  //   388
  //   295
  //   295
  //   B
  //   A
  //   228
  //   180
  //   178
  //   181
  //   232
  //   230
  //   233
  //   235
  //   291
  //   343
  //   !
  //   NEGEDGE
  //   SIPO SR 4bit
  //   SIPO SR 4bit
  //   392
  //   209
endmodule

// COUNTER 1BIT
module _1_bit_cnt (
  input  C,
  input  CIN,
  input  VAL,
  input  nLD,
  input  nRES,
  output Q,
  output nQ,
  output CO
);

  wire d_ff_1_q, multiplexer_1_out, not_1_out, not_2_out, xor_1_out;

  not not_1 (not_1_out, nRES);
  xor xor_1 (xor_1_out, Q, CIN);
  and and_1 (CO, Q, CIN);
  Multiplexer #(.disabled(0), .enable("false")) multiplexer_1 (
    .in0(VAL), .in1(xor_1_out), .out(multiplexer_1_out), .sel(nLD));
  not not_2 (not_2_out, C);
  D_Flip_Flop #(.trigger("high")) d_ff_1 (
    .clk(C), .D(multiplexer_1_out), .Q(d_ff_1_q), .reset(not_1_out));  // open: Qn, preset, en
  D_Flip_Flop #(.trigger("high")) d_ff_2 (
    .clk(not_2_out), .D(d_ff_1_q), .Q(Q), .Qn(nQ), .reset(not_1_out));  // open: preset, en

  // Notes on the sheet:
  //   C
  //   VAL
  //   LD
  //   /RES
  //   CIN
  //   CNT BIT
  //   Q
  //   nQ
  //   CO
endmodule

module RC_DELAY (
  input  IN,
  output OUT
);

  wire xor_1_out, xor_2_out, xor_3_out, xor_4_out, xor_5_out;

  xor xor_1 (xor_1_out, IN, 1'b0);
  xor xor_2 (xor_2_out, xor_1_out, 1'b0);
  xor xor_3 (xor_3_out, xor_2_out, 1'b0);
  xor xor_4 (xor_4_out, xor_3_out, 1'b0);
  xor xor_5 (xor_5_out, xor_4_out, 1'b0);
  xor xor_6 (OUT, xor_5_out, 1'b0);
endmodule

module S_latch (
  input  EN,
  input  D,
  output Q,
  output nQ
);

  D_Flip_Flop #(.trigger("high")) d_ff_1 (.clk(EN), .D(D), .Q(Q), .Qn(nQ));  // open: preset, en, reset
endmodule
